# Fritzing sketch DR4018_5_sein3 (saved by Fritzing 0.9.3b)

parts:
  Onderdeel1 = DR4018
  Sein1 = Sein3
  Sein2 = Sein3
  Sein3 = Sein3
  Sein4 = Sein3
  Sein5 = Sein3

nets:
  N1: Onderdeel1.C#15, Sein1.COMMON
  N2: Onderdeel1.3, Onderdeel1.8, Sein1.GREEN
  N3: Onderdeel1.C#18, Onderdeel1.4, Onderdeel1.7, Sein2.COMMON
  N4: Onderdeel1.6, Sein2.GREEN
  N5: Onderdeel1.C#27, Sein3.COMMON
  N6: Onderdeel1.9, Sein3.GREEN
  N7: Onderdeel1.C#33, Sein4.COMMON
  N8: Onderdeel1.12, Sein4.GREEN
  N9: Onderdeel1.C#36, Sein5.COMMON
  N10: Onderdeel1.15, Sein5.GREEN
